# Fritzing sketch circuit (saved by Fritzing 0.9.3b)
breadboards: 2

parts:
  Part1 = Arduino Uno (Rev3)
  Part2 = Arduino Due (Rev2b)  # not connected
  U1 = MLX90614 [package=to-39]
  R1 = Resistor [tolerance=±5% resistance=220 package=THT]
  R2 = Resistor [tolerance=±5% resistance=220 package=THT]
  S1 = Pushbutton [package="[SMD]"]

nets:
  N1: Part1.A4/SDA, U1.VSS, R1.Pin_0
  N2: Part1.A5/SCL, U1.VDD, R2.Pin_0
  N3: Part1.D2, S1.Pin_1, S1.Pin_2
  N4: Part1.3V3, U1.SCL_VZ, R1.Pin_1, R2.Pin_1
  N5: Part1.GND, U1.PWM_SDA, S1.Pin_3, S1.Pin_4
